# Fritzing sketch KeyPad3x4 (saved by Fritzing 0.9.5d)
breadboards: 1

parts:
  Part1 = Arduino Uno (Rev3) - ICSP
  S1 = Toggle Switch [package=THT]
  kEYPAD_MATRICIAL_1 = KEYPAD 4x3

nets:
  GND: Part1.GND, S1.L2
  N1: Part1.D8, kEYPAD_MATRICIAL_1.arrow3
  N2: Part1.D9_PWM, kEYPAD_MATRICIAL_1.arrow2
  N3: Part1.D10_PWM/SS, S1.COM
  N4: Part1.D3_PWM, kEYPAD_MATRICIAL_1.col2
  N5: Part1.D4, kEYPAD_MATRICIAL_1.col1
  N6: Part1.D5_PWM, kEYPAD_MATRICIAL_1.col3
  N7: Part1.D6_PWM, kEYPAD_MATRICIAL_1.arrow1
  N8: Part1.D7, kEYPAD_MATRICIAL_1.arrow4
  N9: Part1.5V, S1.L1

custom parts:
  KEYPAD 4x3: KEYPAD matricial de 12 botones, 4 filas x 3 columnas
